// Logisim project DZ27.10.circ as structural Verilog
module Mur_Double (
  input  inp,
  output out_2
);

  wire and_1_out, and_2_out, clock_1_out, d_ff_1_q, d_ff_2_q, d_ff_3_q, not_1_out, not_2_out, not_3_out,
       not_4_out, not_5_out, not_6_out, not_7_out, not_8_out, not_9_out, not_10_out, or_1_out, Q0_out,
       Q1_out, Q2_out, xor_1_out, xor_2_out;

  not not_1 (not_1_out, d_ff_1_q);
  and Q2 (Q2_out, not_1_out, d_ff_2_q, d_ff_3_q, inp);
  xor xor_1 (xor_1_out, d_ff_2_q, d_ff_3_q);
  not not_2 (not_2_out, d_ff_2_q);
  not not_3 (not_3_out, d_ff_1_q);
  not not_4 (not_4_out, inp);
  not not_5 (not_5_out, d_ff_3_q);
  xor xor_2 (xor_2_out, d_ff_2_q, d_ff_1_q);
  not not_6 (not_6_out, d_ff_1_q);
  not not_7 (not_7_out, inp);
  or or_1 (or_1_out, not_2_out, not_3_out);
  not not_8 (not_8_out, d_ff_3_q);
  and and_1 (and_1_out, not_4_out, not_5_out, xor_2_out);
  and Q1 (Q1_out, not_6_out, not_7_out, xor_1_out);
  and and_2 (and_2_out, or_1_out, not_8_out, inp);
  or Q0 (Q0_out, and_2_out, and_1_out);
  Clock clock_1 (.out(clock_1_out));
  D_Flip_Flop d_ff_1 (.D(Q2_out), .clk(clock_1_out), .Q(d_ff_1_q));  // open: Qn, preset, reset
  D_Flip_Flop d_ff_2 (.D(Q1_out), .clk(clock_1_out), .Q(d_ff_2_q));  // open: Qn, preset, reset
  D_Flip_Flop d_ff_3 (.D(Q0_out), .clk(clock_1_out), .Q(d_ff_3_q));  // open: Qn, preset, reset
  not not_9 (not_9_out, d_ff_2_q);
  not not_10 (not_10_out, d_ff_3_q);
  and and_3 (out_2, d_ff_1_q, not_9_out, not_10_out);
  // NOT_Gate not_11 is placed but not wired

  // Notes on the sheet:
  //   Q2
  //   Q1
  //   Q0
endmodule

module Mur_NotDouble (
  input  inp,
  output out_2
);

  wire and_1_out, and_2_out, and_3_out, and_4_out, clock_1_out, d_ff_1_q, d_ff_2_q, d_ff_3_q, d_ff_4_q,
       d_ff_5_q, not_1_out, not_2_out, not_3_out, not_4_out, not_5_out, not_6_out, not_7_out, not_8_out,
       or_1_out, or_2_out, Q0_out, Q1_out, Q2_out, Q3_out, Q4_out;

  not not_1 (not_1_out, inp);
  or or_1 (or_1_out, d_ff_1_q, d_ff_4_q);
  not not_2 (not_2_out, inp);
  or or_2 (or_2_out, d_ff_3_q, d_ff_2_q, d_ff_1_q);
  and and_1 (and_1_out, inp, d_ff_5_q);
  and and_2 (and_2_out, not_1_out, or_1_out);
  and and_3 (and_3_out, not_2_out, d_ff_5_q);
  and and_4 (and_4_out, inp, or_2_out);
  not not_3 (not_3_out, inp);
  not not_4 (not_4_out, inp);
  or Q0 (Q0_out, and_1_out, and_2_out);
  or Q1 (Q1_out, and_3_out, and_4_out);
  and Q2 (Q2_out, not_3_out, d_ff_2_q);
  and Q3 (Q3_out, not_4_out, d_ff_3_q);
  and Q4 (Q4_out, inp, d_ff_4_q);
  Clock clock_1 (.out(clock_1_out));
  D_Flip_Flop d_ff_1 (.D(Q0_out), .clk(clock_1_out), .Q(d_ff_1_q));  // open: Qn, preset, reset
  D_Flip_Flop d_ff_2 (.D(Q1_out), .clk(clock_1_out), .Q(d_ff_2_q));  // open: Qn, preset, reset
  D_Flip_Flop d_ff_3 (.D(Q2_out), .clk(clock_1_out), .Q(d_ff_3_q));  // open: Qn, preset, reset
  D_Flip_Flop d_ff_4 (.D(Q3_out), .clk(clock_1_out), .Q(d_ff_4_q));  // open: Qn, preset, reset
  D_Flip_Flop d_ff_5 (.D(Q4_out), .clk(clock_1_out), .Q(d_ff_5_q));  // open: Qn, preset, reset
  not not_5 (not_5_out, d_ff_1_q);
  not not_6 (not_6_out, d_ff_2_q);
  not not_7 (not_7_out, d_ff_3_q);
  not not_8 (not_8_out, d_ff_4_q);
  and res (out_2, not_5_out, not_6_out, not_7_out, not_8_out, d_ff_5_q);

  // Notes on the sheet:
  //   Q3
  //   Q4
  //   Q1
  //   Q2
  //   Q0
endmodule

module MILI_Double (
  input  in_1,
  output out_2
);

  wire and_1_out, clock_1_out, d_ff_1_q, d_ff_2_q, not_1_out, not_2_out, Q0_out, Q1_out, xor_1_out;

  not not_1 (not_1_out, in_1);
  xor xor_1 (xor_1_out, d_ff_1_q, d_ff_2_q);
  not not_2 (not_2_out, in_1);
  and and_1 (and_1_out, d_ff_1_q, not_1_out);
  and Q1 (Q1_out, xor_1_out, not_2_out);
  or Q0 (Q0_out, and_1_out, in_1);
  Clock clock_1 (.out(clock_1_out));
  D_Flip_Flop d_ff_1 (.D(Q1_out), .clk(clock_1_out), .Q(d_ff_1_q));  // open: Qn, preset, reset
  D_Flip_Flop d_ff_2 (.D(Q0_out), .clk(clock_1_out), .Q(d_ff_2_q));  // open: Qn, preset, reset
  and and_2 (out_2, d_ff_1_q, d_ff_2_q, in_1);

  // Notes on the sheet:
  //   Q1
  //   Q0
endmodule

module MILI_NotDouble (
  input  inp,
  output out_2
);

  wire and_1_out, and_2_out, clock_1_out, d_ff_1_q, d_ff_2_q, d_ff_3_q, d_ff_4_q, not_1_out, not_2_out,
       not_3_out, Q0_out, Q1_out, Q2_out, Q3_out;

  not not_1 (not_1_out, inp);
  not not_2 (not_2_out, inp);
  not not_3 (not_3_out, inp);
  and and_1 (and_1_out, d_ff_1_q, inp);
  and and_2 (and_2_out, d_ff_4_q, not_1_out);
  and Q3 (Q3_out, d_ff_2_q, not_2_out);
  and Q2 (Q2_out, d_ff_3_q, not_3_out);
  xor Q1 (Q1_out, d_ff_1_q, inp);
  or Q0 (Q0_out, and_1_out, and_2_out);
  Clock clock_1 (.out(clock_1_out));
  D_Flip_Flop d_ff_1 (.D(Q3_out), .clk(clock_1_out), .Q(d_ff_1_q));  // open: Qn, preset, reset
  D_Flip_Flop d_ff_2 (.D(Q2_out), .clk(clock_1_out), .Q(d_ff_2_q));  // open: Qn, preset, reset
  D_Flip_Flop d_ff_3 (.D(Q1_out), .clk(clock_1_out), .Q(d_ff_3_q));  // open: Qn, preset, reset
  D_Flip_Flop d_ff_4 (.D(Q0_out), .clk(clock_1_out), .Q(d_ff_4_q));  // open: Qn, preset, reset
  and and_3 (out_2, d_ff_4_q, inp);

  // Notes on the sheet:
  //   Q3
  //   Q2
  //   Q1
  //   Q0
endmodule
