// Logisim project Zad2.circ as structural Verilog: 7 circuits, main circuit ALU
module ALU (
  input  [2:0] in_1,
  input  [31:0] A,
  input  [31:0] B,
  output [31:0] out_4,
  output Zero,
  output Negative
);

  wire bitselector_1_out, iszero_1_out_2;
  wire [31:0] adder_1_out, and_1_out, bit_extender_1_out, multiplexer_1_out, not_1_out, or_1_out;

  assign not_1_out = ~B;  // NOT_Gate not_1, 32 bits wide
  Multiplexer #(.width(32), .enable("false")) multiplexer_1 (
    .in0(B), .in1(not_1_out), .out(multiplexer_1_out), .sel(in_1[2]));
  Adder #(.width(32)) adder_1 (.a(multiplexer_1_out), .b(A), .out(adder_1_out), .cin(in_1[2]));  // open: cout
  assign and_1_out = multiplexer_1_out & A;  // AND_Gate and_1, 32 bits wide
  assign or_1_out = multiplexer_1_out | A;  // OR_Gate or_1, 32 bits wide
  BitSelector #(.width(32)) bitselector_1 (.in(adder_1_out), .out(bitselector_1_out), .sel({5{1'b1}}));
  assign bit_extender_1_out = {{31{bitselector_1_out}}, bitselector_1_out};  // Bit_Extender bit_extender_1
  Multiplexer #(.select(2), .width(32), .enable("false")) multiplexer_2 (
    .in0(and_1_out), .in1(or_1_out), .in2(adder_1_out), .in3(bit_extender_1_out), .out(out_4), .sel(in_1[1:0]));
  IsZero iszero_1 (.in_1(out_4), .out_2(iszero_1_out_2));
  not not_2 (Zero, iszero_1_out_2);
  BitSelector #(.width(32)) bitselector_2 (.in(out_4), .out(Negative), .sel({5{1'b1}}));
endmodule

module IsZero (
  input  [31:0] in_1,
  output out_2
);

  or or_1 (out_2, in_1[0], in_1[1], in_1[2], in_1[3], in_1[4], in_1[5], in_1[6], in_1[7], in_1[8], in_1[9], in_1[10], in_1[11], in_1[12], in_1[13], in_1[14], in_1[15], in_1[17], in_1[18], in_1[19], in_1[20], in_1[21], in_1[22], in_1[23], in_1[24], in_1[25], in_1[26], in_1[27], in_1[28], in_1[29], in_1[30], in_1[31], in_1[16]);
endmodule

module ALUL (
  input  [15:0] A,
  input  [15:0] B,
  input  zx,
  input  nx,
  input  zy,
  input  nz,
  input  f,
  input  no,
  output [15:0] Out1,
  output zero,
  output negative
);

  wire iszero16_1_out_2;
  wire [15:0] adder_1_out, and_1_out, multiplexer_1_out, multiplexer_2_out, multiplexer_3_out,
       multiplexer_4_out, multiplexer_5_out, not_1_out, not_2_out, not_3_out;

  Multiplexer #(.width(16), .enable("false")) multiplexer_1 (
    .in0(A), .in1({16{1'b0}}), .out(multiplexer_1_out), .sel(zx));
  assign not_1_out = ~multiplexer_1_out;  // NOT_Gate not_1, 16 bits wide
  Multiplexer #(.width(16), .enable("false")) multiplexer_2 (
    .in0(multiplexer_1_out), .in1(not_1_out), .out(multiplexer_2_out), .sel(nx));
  Multiplexer #(.width(16), .enable("false")) multiplexer_3 (
    .in0(B), .in1({16{1'b0}}), .out(multiplexer_3_out), .sel(zy));
  assign not_2_out = ~multiplexer_3_out;  // NOT_Gate not_2, 16 bits wide
  Multiplexer #(.width(16), .enable("false")) multiplexer_4 (
    .in0(multiplexer_3_out), .in1(not_2_out), .out(multiplexer_4_out), .sel(nz));
  Adder #(.width(16)) adder_1 (.a(multiplexer_4_out), .b(multiplexer_2_out), .out(adder_1_out));  // open: cin, cout
  assign and_1_out = multiplexer_4_out & multiplexer_2_out;  // AND_Gate and_1, 16 bits wide
  Multiplexer #(.width(16), .enable("false")) multiplexer_5 (
    .in0(and_1_out), .in1(adder_1_out), .out(multiplexer_5_out), .sel(f));
  assign not_3_out = ~multiplexer_5_out;  // NOT_Gate not_3, 16 bits wide
  Multiplexer #(.width(16), .enable("false")) multiplexer_6 (
    .in0(multiplexer_5_out), .in1(not_3_out), .out(Out1), .sel(no));
  IsZero16 iszero16_1 (.in_1(Out1), .out_2(iszero16_1_out_2));
  BitSelector #(.width(16)) bitselector_1 (.in(Out1), .out(negative), .sel(4'b1111));
  not not_4 (zero, iszero16_1_out_2);
endmodule

module IsZero16 (
  input  [15:0] in_1,
  output out_2
);

  or or_1 (out_2, in_1[0], in_1[1], in_1[2], in_1[3], in_1[4], in_1[5], in_1[6], in_1[7], in_1[9], in_1[10], in_1[11], in_1[12], in_1[13], in_1[14], in_1[15], in_1[8]);
endmodule

module logicalShifter (
  input  [1:0] shamt,
  input  [3:0] inp,
  output [3:0] out_3
);

  Multiplexer #(.select(2), .enable("false")) multiplexer_1 (
    .in0(inp[3]), .in1(inp[2]), .in2(inp[1]), .in3(inp[0]), .out(out_3[3]), .sel(shamt));
  Multiplexer #(.select(2), .enable("false")) multiplexer_2 (
    .in0(inp[2]), .in1(inp[1]), .in2(inp[0]), .in3(1'b0), .out(out_3[2]), .sel(shamt));
  Multiplexer #(.select(2), .enable("false")) multiplexer_3 (
    .in0(inp[1]), .in1(inp[0]), .in2(1'b0), .in3(1'b0), .out(out_3[1]), .sel(shamt));
  Multiplexer #(.select(2), .enable("false")) multiplexer_4 (
    .in0(inp[0]), .in1(1'b0), .in2(1'b0), .in3(1'b0), .out(out_3[0]), .sel(shamt));
endmodule

module logicalShifterR (
  input  [1:0] in_1,
  input  [3:0] in_2,
  output [3:0] out_3
);

  Multiplexer #(.select(2), .enable("false")) multiplexer_1 (
    .in0(in_2[0]), .in1(in_2[1]), .in2(in_2[2]), .in3(in_2[3]), .out(out_3[0]), .sel(in_1));
  Multiplexer #(.select(2), .enable("false")) multiplexer_2 (
    .in0(in_2[1]), .in1(in_2[2]), .in2(in_2[3]), .in3(1'b0), .out(out_3[1]), .sel(in_1));
  Multiplexer #(.select(2), .enable("false")) multiplexer_3 (
    .in0(in_2[2]), .in1(in_2[3]), .in2(1'b0), .in3(1'b0), .out(out_3[2]), .sel(in_1));
  Multiplexer #(.select(2), .enable("false")) multiplexer_4 (
    .in0(in_2[3]), .in1(1'b0), .in2(1'b0), .in3(1'b0), .out(out_3[3]), .sel(in_1));
endmodule

module ArifmetShifterR (
  input  [1:0] in_1,
  input  [3:0] in_2,
  output [3:0] out_3
);

  Multiplexer #(.select(2), .enable("false")) multiplexer_1 (
    .in0(in_2[3]), .in1(in_2[3]), .in2(in_2[3]), .in3(in_2[3]), .out(out_3[3]), .sel(in_1));
  Multiplexer #(.select(2), .enable("false")) multiplexer_2 (
    .in0(in_2[2]), .in1(in_2[3]), .in2(in_2[3]), .in3(in_2[3]), .out(out_3[2]), .sel(in_1));
  Multiplexer #(.select(2), .enable("false")) multiplexer_3 (
    .in0(in_2[1]), .in1(in_2[2]), .in2(in_2[3]), .in3(in_2[3]), .out(out_3[1]), .sel(in_1));
  Multiplexer #(.select(2), .enable("false")) multiplexer_4 (
    .in0(in_2[0]), .in1(in_2[1]), .in2(in_2[2]), .in3(in_2[3]), .out(out_3[0]), .sel(in_1));
endmodule
