// Logisim project Zad_3..circ as structural Verilog: 21 circuits, main circuit SR_Latch
module SR_Latch (
  input  R,
  input  S,
  output Q,
  output Q0
);

  nor nor_1 (Q, R, Q0);
  nor nor_2 (Q0, Q, S);
endmodule

module D_Latch (
  input  CLK,
  input  D,
  output Q,
  output Q0
);

  wire and_1_out, and_2_out, not_1_out;

  and and_1 (and_1_out, CLK, not_1_out);
  not not_1 (not_1_out, D);
  and and_2 (and_2_out, CLK, D);
  SR_Latch sr_latch_1 (.Q(Q), .Q0(Q0), .S(and_2_out), .R(and_1_out));
endmodule

module D_Flip_Flop (
  input  CLK,
  input  D,
  output Q
);

  wire d_latch_1_q, not_1_out;

  not not_1 (not_1_out, CLK);
  D_Latch d_latch_1 (.Q(d_latch_1_q), .D(D), .CLK(not_1_out));  // open: Q0
  D_Latch d_latch_2 (.Q(Q), .D(d_latch_1_q), .CLK(CLK));  // open: Q0
endmodule

module Enabled_Flip_Flop (
  input  CLK,
  input  EN,
  input  D,
  output Q
);

  wire and_1_out;

  and and_1 (and_1_out, CLK, EN);
  D_Flip_Flop d_flip_flop_1 (.Q(Q), .CLK(and_1_out), .D(D));
endmodule

module Resettable_Flip_Flop (
  input  CLK,
  input  D,
  input  RESET,
  output Q
);

  wire and_1_out, not_1_out;

  not not_1 (not_1_out, RESET);
  and and_1 (and_1_out, D, not_1_out);
  D_Flip_Flop d_flip_flop_1 (.Q(Q), .CLK(CLK), .D(and_1_out));
endmodule

module async_reset_D_Latch (
  input  CLK,
  input  D,
  input  Reset,
  output out_4,
  output out_5
);

  wire and_1_out, and_2_out, not_1_out, not_2_out, not_3_out, or_1_out, or_2_out;

  not not_1 (not_1_out, D);
  or or_1 (or_1_out, CLK, Reset);
  or or_2 (or_2_out, not_1_out, Reset);
  not not_2 (not_2_out, or_2_out);
  and and_1 (and_1_out, or_1_out, not_3_out);
  not not_3 (not_3_out, not_2_out);
  and and_2 (and_2_out, or_1_out, not_2_out);
  SR_Latch sr_latch_1 (.Q(out_4), .Q0(out_5), .S(and_2_out), .R(and_1_out));
endmodule

module async_resettable_Flip_Flop_V2 (
  input  CLK,
  input  D,
  input  Reset,
  output Q
);

  wire async_reset_d_latch_1_out_4, not_1_out;

  async_reset_D_Latch async_reset_d_latch_1 (
    .Reset(Reset), .out_4(async_reset_d_latch_1_out_4), .CLK(not_1_out), .D(D));  // open: out_5
  not not_1 (not_1_out, CLK);
  async_reset_D_Latch async_reset_d_latch_2 (
    .Reset(Reset), .out_4(Q), .CLK(CLK), .D(async_reset_d_latch_1_out_4));  // open: out_5
endmodule

module Async_reset_Flip_Flop_down (
  input  CLK,
  input  D,
  input  Reset,
  output Q
);

  wire and_1_out, d_latch_1_q, d_latch_2_q, not_1_out, not_2_out, or_1_out, sr_latch_1_q;

  D_Latch d_latch_1 (.Q(d_latch_1_q), .D(D), .CLK(CLK));  // open: Q0
  not not_1 (not_1_out, CLK);
  SR_Latch sr_latch_1 (.Q(sr_latch_1_q), .S(Reset), .R(CLK));  // open: Q0
  and and_1 (and_1_out, d_latch_1_q, not_2_out);
  not not_2 (not_2_out, or_1_out);
  D_Latch d_latch_2 (.Q(d_latch_2_q), .D(and_1_out), .CLK(not_1_out));  // open: Q0
  and and_2 (Q, d_latch_2_q, not_2_out);
  or or_1 (or_1_out, sr_latch_1_q, Reset);
endmodule

module thing (
  input  in_1,
  input  in_2,
  input  in_3,
  output out_4
);

  wire and_1_out, d_latch_1_q, d_latch_2_q, not_1_out, not_2_out, or_1_out, or_2_out, sr_latch_1_q;

  not not_1 (not_1_out, in_1);
  D_Latch d_latch_1 (.Q(d_latch_1_q), .D(in_2), .CLK(not_1_out));  // open: Q0
  SR_Latch sr_latch_1 (.Q(sr_latch_1_q), .S(in_3), .R(in_1));  // open: Q0
  and and_1 (and_1_out, d_latch_1_q, not_2_out);
  or or_1 (or_1_out, in_1, or_2_out);
  D_Latch d_latch_2 (.Q(d_latch_2_q), .D(and_1_out), .CLK(or_1_out));  // open: Q0
  not not_2 (not_2_out, or_2_out);
  or or_2 (or_2_out, sr_latch_1_q, in_3);
  and and_2 (out_4, d_latch_2_q, not_2_out);
endmodule

module Set_Flip_Flop (
  input  CLK,
  input  D,
  input  Set,
  output Q
);

  wire or_1_out;

  or or_1 (or_1_out, D, Set);
  D_Flip_Flop d_flip_flop_1 (.Q(Q), .CLK(CLK), .D(or_1_out));
endmodule

module Set_async_D_Latch (
  input  CLK,
  input  SET,
  input  D,
  output Q,
  output Q0
);

  wire and_1_out, and_2_out, not_1_out, or_1_out, or_2_out;

  or or_1 (or_1_out, CLK, SET);
  or or_2 (or_2_out, SET, D);
  and and_1 (and_1_out, or_1_out, not_1_out);
  not not_1 (not_1_out, or_2_out);
  and and_2 (and_2_out, or_1_out, or_2_out);
  SR_Latch sr_latch_1 (.Q(Q), .Q0(Q0), .S(and_2_out), .R(and_1_out));
endmodule

module async_set_Flip_Flop (
  input  CLK,
  input  D,
  input  Set,
  output Q
);

  wire not_1_out, set_async_d_latch_1_q;

  not not_1 (not_1_out, CLK);
  Set_async_D_Latch set_async_d_latch_1 (.Q(set_async_d_latch_1_q), .D(D), .SET(Set), .CLK(not_1_out));  // open: Q0
  Set_async_D_Latch set_async_d_latch_2 (.Q(Q), .D(set_async_d_latch_1_q), .SET(Set), .CLK(CLK));  // open: Q0
endmodule

module D_trigger (
  input  CLK,
  input  D,
  input  enable,
  input  set,
  input  reset,
  output Q
);

  wire async_set_flip_flop_1_q, d_latch_1_q, enabled_flip_flop_1_q, g, not_1_out, not_2_out, not_3_out,
       or_1_out, or_2_out, or_3_out, or_4_out, or_5_out, set_async_d_latch_1_q, set_async_d_latch_2_q;

  and and_1 (g, CLK, not_1_out, enable);
  not not_1 (not_1_out, D);
  or or_1 (or_1_out, CLK, reset);
  Enabled_Flip_Flop enabled_flip_flop_1 (.Q(enabled_flip_flop_1_q), .EN(or_2_out), .D(D), .CLK(or_1_out));
  or or_2 (or_2_out, enable, reset);
  async_set_Flip_Flop async_set_flip_flop_1 (.Q(async_set_flip_flop_1_q), .Set(set), .CLK(CLK));  // open: D
  or or_3 (or_3_out, set, CLK);
  not not_2 (not_2_out, or_3_out);
  Set_async_D_Latch set_async_d_latch_1 (.Q(set_async_d_latch_1_q), .SET(reset), .CLK(not_2_out));  // open: Q0, D
  or or_4 (or_4_out, async_set_flip_flop_1_q, g, set_async_d_latch_2_q);
  Set_async_D_Latch set_async_d_latch_2 (
    .Q(set_async_d_latch_2_q), .D(set_async_d_latch_1_q), .SET(reset), .CLK(or_3_out));  // open: Q0
  D_Latch d_latch_1 (.Q(d_latch_1_q), .D(async_set_flip_flop_1_q), .CLK(or_4_out));  // open: Q0
  not not_3 (not_3_out, set_async_d_latch_2_q);
  or or_5 (or_5_out, d_latch_1_q, enabled_flip_flop_1_q);
  and and_2 (Q, not_3_out, or_5_out);
endmodule

module D_trigger_2 (
  input  in_1,
  input  in_2,
  input  in_3,
  input  in_4,
  input  in_5,
  input  in_6,
  input  in_7,
  input  in_8,
  input  CLK,
  input  EN,
  input  D,
  input  Set,
  input  Reset,
  output out_14,
  output out_15,
  output Q
);

  wire and_1_out, multiplexer_1_out, not_1_out, not_2_out, or_1_out, or_2_out;

  not not_1 (not_1_out, Set);
  or or_1 (or_1_out, not_1_out, Reset);
  or or_2 (or_2_out, Reset, Set);
  not not_2 (not_2_out, or_1_out);
  D_Flip_Flop_part d_ff_1 (.D(in_2), .clk(in_5), .Q(out_14), .preset(in_1), .reset(in_7));  // open: Qn
  Multiplexer #(.enable("false")) multiplexer_1 (.in0(D), .in1(not_2_out), .out(multiplexer_1_out), .sel(or_2_out));
  and and_1 (and_1_out, CLK, EN);
  D_Flip_Flop d_flip_flop_1 (.Q(Q), .CLK(and_1_out), .D(multiplexer_1_out));
  Register #(.width(1)) register_1 (.D(in_3), .en(in_4), .clk(in_6), .Q(out_15), .clr(in_8));
endmodule

module D_trigger_3 (
  input  in_1,
  input  in_2,
  input  in_3,
  input  in_4,
  input  in_5,
  output out_6
);

  wire async_reset_d_latch_1_out_4, async_set_flip_flop_1_q, enabled_flip_flop_1_q;

  Enabled_Flip_Flop enabled_flip_flop_1 (.Q(enabled_flip_flop_1_q), .EN(in_3), .D(in_2), .CLK(in_1));
  async_reset_D_Latch async_reset_d_latch_1 (
    .Reset(in_5), .out_4(async_reset_d_latch_1_out_4), .CLK(in_1));  // open: out_5, D
  async_set_Flip_Flop async_set_flip_flop_1 (.Q(async_set_flip_flop_1_q), .Set(in_4), .CLK(in_1));  // open: D
endmodule

module PC (
  input  [15:0] inp,
  input  reset,
  input  load,
  input  inc,
  output [15:0] o
);

  wire and_1_out, clock_1_out, not_1_out, or_1_out;
  wire [15:0] adder_1_out, multiplexer_1_out, multiplexer_2_out;

  Multiplexer #(.width(16), .enable("false")) multiplexer_1 (.in0(o), .in1(inp), .out(multiplexer_1_out), .sel(load));
  not not_1 (not_1_out, load);
  Adder #(.width(16)) adder_1 (.a(multiplexer_1_out), .b(16'h1), .out(adder_1_out));  // open: cin, cout
  and and_1 (and_1_out, not_1_out, inc);
  Register #(.width(16)) register_1 (.D(multiplexer_2_out), .en(or_1_out), .clk(clock_1_out), .Q(o), .clr(reset));
  Multiplexer #(.width(16), .enable("false")) multiplexer_2 (
    .in0(multiplexer_1_out), .in1(adder_1_out), .out(multiplexer_2_out), .sel(and_1_out));
  Clock clock_1 (.out(clock_1_out));
  or or_1 (or_1_out, load, and_1_out, reset);
endmodule

module trigger_4bit (
  input  [3:0] in_1,
  input  in_2,
  input  in_3,
  input  in_4,
  output [3:0] out_5
);

  wire clock_1_out;

  Clock clock_1 (.out(clock_1_out));
  D_trigger d_trigger_1 (.reset(in_4), .set(in_2), .enable(in_3), .D(in_1[0]), .CLK(clock_1_out), .Q(out_5[0]));
  D_trigger d_trigger_2 (.reset(in_4), .set(in_2), .enable(in_3), .D(in_1[1]), .CLK(clock_1_out), .Q(out_5[1]));
  D_trigger d_trigger_3 (.reset(in_4), .set(in_2), .enable(in_3), .D(in_1[2]), .CLK(clock_1_out), .Q(out_5[2]));
  D_trigger d_trigger_4 (.reset(in_4), .set(in_2), .enable(in_3), .D(in_1[3]), .CLK(clock_1_out), .Q(out_5[3]));
endmodule

module Ex_13 (
  input  [7:0] A,
  input  [7:0] B,
  input  C
);

  wire clock_1_out;
  wire [7:0] adder_1_out, register_1_q, register_2_q, xor_1_out;

  assign xor_1_out = A ^ B;  // XOR_Gate xor_1, 8 bits wide
  Clock clock_1 (.out(clock_1_out));
  Adder adder_1 (.a(register_2_q), .b(xor_1_out), .out(adder_1_out), .cin(C));  // open: cout
  Register register_1 (.D(adder_1_out), .en(1'b1), .clk(clock_1_out), .Q(register_1_q));  // open: clr
  Register register_2 (.D(register_1_q), .en(1'b1), .clk(clock_1_out), .Q(register_2_q));  // open: clr

  // Notes on the sheet:
  //   Ответы R1 и R2
  //   Ответы R1 и R2
endmodule

module Ex_14 (
  input  [7:0] I,
  output [7:0] O
);

  wire button_1_out, clock_1_out;
  wire [7:0] adder_1_out, multiplexer_1_out, not_1_out;

  Clock clock_1 (.out(clock_1_out));
  Register register_1 (.D(adder_1_out), .en(clock_1_out), .clk(clock_1_out), .Q(O));  // open: clr
  Multiplexer #(.width(8), .enable("false")) multiplexer_1 (
    .in0(I), .in1(not_1_out), .out(multiplexer_1_out), .sel(button_1_out));
  assign not_1_out = ~I;  // NOT_Gate not_1, 8 bits wide
  Button button_1 (.out(button_1_out));
  Adder adder_1 (.a(O), .b(multiplexer_1_out), .out(adder_1_out), .cin(button_1_out));  // open: cout
endmodule

module Ram8 (
  input  [31:0] I,
  input  [2:0] address,
  input  load,
  output [31:0] O
);

  wire a0, a1, a2, a3, a4, a5, a6, a7;
  wire [31:0] b0, b1, b2, b3, b4, b5, b6, b7, register_1_q, register_2_q, register_3_q, register_4_q,
       register_5_q, register_6_q, register_7_q, register_8_q;

  Demultiplexer #(.select(3), .enable("false")) demultiplexer_1 (
    .out0(a0), .out1(a1), .out2(a2), .out3(a3), .out4(a4), .out5(a5), .out6(a6), .out7(a7), .in(load),
    .sel(address));
  Demultiplexer #(.select(3), .width(32), .enable("false")) demultiplexer_2 (
    .out0(b0), .out1(b1), .out2(b2), .out3(b3), .out4(b4), .out5(b5), .out6(b6), .out7(b7), .in(I),
    .sel(address));
  Register #(.width(32)) register_1 (.D(b0), .en(a0), .clk(a0), .Q(register_1_q));  // open: clr
  Register #(.width(32)) register_2 (.D(b1), .en(a1), .clk(a1), .Q(register_2_q));  // open: clr
  Register #(.width(32)) register_3 (.D(b2), .en(a2), .clk(a2), .Q(register_3_q));  // open: clr
  Register #(.width(32)) register_4 (.D(b3), .en(a3), .clk(a3), .Q(register_4_q));  // open: clr
  Register #(.width(32)) register_5 (.D(b4), .en(a4), .clk(a4), .Q(register_5_q));  // open: clr
  Register #(.width(32)) register_6 (.D(b5), .en(a5), .clk(a5), .Q(register_6_q));  // open: clr
  Register #(.width(32)) register_7 (.D(b6), .en(a6), .clk(a6), .Q(register_7_q));  // open: clr
  Register #(.width(32)) register_8 (.D(b7), .en(a7), .clk(a7), .Q(register_8_q));  // open: clr
  Multiplexer #(.select(3), .width(32), .enable("false")) multiplexer_1 (
    .in0(register_1_q), .in1(register_2_q), .in2(register_3_q), .in3(register_4_q), .in4(register_5_q),
    .in5(register_6_q), .in6(register_7_q), .in7(register_8_q), .out(O), .sel(address));

  // Other names for the same wires on the sheet: a[2:0] = address
endmodule

module RAM64 (
  input  [31:0] in_1,
  input  [5:0] in_2,
  output [31:0] out_3
);

  wire clock_1_out;
  wire [2:0] a0, a1, a2, a3, a4, a5, a6, a7;
  wire [31:0] b0, b1, b2, b3, b4, b5, b6, b7, ram8_1_o, ram8_2_o, ram8_3_o, ram8_4_o, ram8_5_o, ram8_6_o,
       ram8_7_o, ram8_8_o;

  Demultiplexer #(.select(3), .width(32), .enable("false")) demultiplexer_1 (
    .out0(b0), .out1(b1), .out2(b2), .out3(b3), .out4(b4), .out5(b5), .out6(b6), .out7(b7), .in(in_1),
    .sel(in_2[5:3]));
  Demultiplexer #(.select(3), .width(3), .enable("false")) demultiplexer_2 (
    .out0(a0), .out1(a1), .out2(a2), .out3(a3), .out4(a4), .out5(a5), .out6(a6), .out7(a7), .in(in_2[2:0]),
    .sel(in_2[5:3]));
  Ram8 ram8_1 (.I(b0), .address(a0), .load(clock_1_out), .O(ram8_1_o));
  Ram8 ram8_2 (.I(b1), .address(a1), .load(clock_1_out), .O(ram8_2_o));
  Ram8 ram8_3 (.I(b2), .address(a2), .load(clock_1_out), .O(ram8_3_o));
  Ram8 ram8_4 (.I(b3), .address(a3), .load(clock_1_out), .O(ram8_4_o));
  Clock clock_1 (.out(clock_1_out));
  Ram8 ram8_5 (.I(b4), .address(a4), .load(clock_1_out), .O(ram8_5_o));
  Ram8 ram8_6 (.I(b5), .address(a5), .load(clock_1_out), .O(ram8_6_o));
  Ram8 ram8_7 (.I(b6), .address(a6), .load(clock_1_out), .O(ram8_7_o));
  Ram8 ram8_8 (.I(b7), .address(a7), .load(clock_1_out), .O(ram8_8_o));
  Multiplexer #(.select(3), .width(32), .enable("false")) multiplexer_1 (
    .in0(ram8_1_o), .in1(ram8_2_o), .in2(ram8_3_o), .in3(ram8_4_o), .in4(ram8_5_o), .in5(ram8_6_o),
    .in6(ram8_7_o), .in7(ram8_8_o), .out(out_3), .sel(in_2[5:3]));

  // Other names for the same wires on the sheet: data[2:0] = in_2[2:0]; address[2:0] = in_2[5:3]
endmodule
