// Logisim project Zad_3.circ as structural Verilog: 13 circuits, main circuit SR_Latch
module SR_Latch (
  input  R,
  input  S,
  output Q,
  output Q0
);

  nor nor_1 (Q, R, Q0);
  nor nor_2 (Q0, Q, S);
endmodule

module D_Latch (
  input  CLK,
  input  D,
  output Q,
  output Q0
);

  wire and_1_out, and_2_out, not_1_out;

  and and_1 (and_1_out, CLK, not_1_out);
  not not_1 (not_1_out, D);
  and and_2 (and_2_out, CLK, D);
  SR_Latch sr_latch_1 (.Q0(Q0), .Q(Q), .S(and_2_out), .R(and_1_out));
endmodule

module D_Flip_Flop (
  input  CLK,
  input  D,
  output Q
);

  wire d_latch_1_q, not_1_out;

  not not_1 (not_1_out, CLK);
  D_Latch d_latch_1 (.Q(d_latch_1_q), .D(D), .CLK(not_1_out));  // open: Q0
  D_Latch d_latch_2 (.Q(Q), .D(d_latch_1_q), .CLK(CLK));  // open: Q0
endmodule

module Enabled_Flip_Flop (
  input  CLK,
  input  EN,
  input  D,
  output Q
);

  wire and_1_out;

  and and_1 (and_1_out, CLK, EN);
  D_Flip_Flop d_flip_flop_1 (.Q(Q), .D(D), .CLK(and_1_out));
endmodule

module Resettable_Flip_Flop (
  input  CLK,
  input  D,
  input  RESET,
  output Q
);

  wire and_1_out, not_1_out;

  not not_1 (not_1_out, RESET);
  and and_1 (and_1_out, D, not_1_out);
  D_Flip_Flop d_flip_flop_1 (.Q(Q), .D(and_1_out), .CLK(CLK));
endmodule

module async_reset_D_Latch (
  input  CLK,
  input  D,
  input  Reset,
  output out_4,
  output out_5
);

  wire and_1_out, and_2_out, not_1_out, not_2_out, not_3_out, or_1_out;

  not not_1 (not_1_out, D);
  or or_1 (or_1_out, not_1_out, Reset);
  not not_2 (not_2_out, or_1_out);
  and and_1 (and_1_out, CLK, not_3_out);
  not not_3 (not_3_out, not_2_out);
  and and_2 (and_2_out, CLK, not_2_out);
  SR_Latch sr_latch_1 (.Q0(out_5), .Q(out_4), .S(and_2_out), .R(and_1_out));
endmodule

module Bad (
  input  CLK,
  input  D,
  input  Reset,
  input  in_4,
  input  in_5,
  input  in_6,
  output Q,
  output out_8
);

  wire and_1_out, d_latch_1_q, d_latch_2_q, not_1_out, not_2_out, or_1_out, sr_latch_1_q, sr_latch_2_q;

  D_Latch d_latch_1 (.Q(d_latch_1_q), .D(D), .CLK(not_1_out));  // open: Q0
  D_Flip_Flop_part d_ff_1 (.D(in_4), .clk(in_5), .Q(out_8), .reset(in_6));  // open: Qn, preset
  not not_1 (not_1_out, CLK);
  SR_Latch sr_latch_1 (.Q(sr_latch_1_q), .S(Reset), .R(CLK));  // open: Q0
  and and_1 (and_1_out, CLK, sr_latch_1_q);
  not not_2 (not_2_out, or_1_out);
  SR_Latch sr_latch_2 (.Q(sr_latch_2_q), .S(Reset), .R(and_1_out));  // open: Q0
  D_Latch d_latch_2 (.Q(d_latch_2_q), .D(d_latch_1_q), .CLK(CLK));  // open: Q0
  and and_2 (Q, d_latch_2_q, not_2_out);
  or or_1 (or_1_out, sr_latch_1_q, sr_latch_2_q);
endmodule

module Async_reset_Flip_Flop_down (
  input  CLK,
  input  D,
  input  Reset,
  output Q
);

  wire and_1_out, d_latch_1_q, d_latch_2_q, not_1_out, not_2_out, or_1_out, sr_latch_1_q;

  D_Latch d_latch_1 (.Q(d_latch_1_q), .D(D), .CLK(CLK));  // open: Q0
  not not_1 (not_1_out, CLK);
  SR_Latch sr_latch_1 (.Q(sr_latch_1_q), .S(Reset), .R(CLK));  // open: Q0
  and and_1 (and_1_out, d_latch_1_q, not_2_out);
  not not_2 (not_2_out, or_1_out);
  D_Latch d_latch_2 (.Q(d_latch_2_q), .D(and_1_out), .CLK(not_1_out));  // open: Q0
  and and_2 (Q, d_latch_2_q, not_2_out);
  or or_1 (or_1_out, sr_latch_1_q, Reset);
endmodule

module thing (
  input  in_1,
  input  in_2,
  input  in_3,
  output out_4
);

  wire and_1_out, d_latch_1_q, d_latch_2_q, not_1_out, not_2_out, or_1_out, or_2_out, sr_latch_1_q;

  not not_1 (not_1_out, in_1);
  D_Latch d_latch_1 (.Q(d_latch_1_q), .D(in_2), .CLK(not_1_out));  // open: Q0
  SR_Latch sr_latch_1 (.Q(sr_latch_1_q), .S(in_3), .R(in_1));  // open: Q0
  and and_1 (and_1_out, d_latch_1_q, not_2_out);
  or or_1 (or_1_out, in_1, or_2_out);
  D_Latch d_latch_2 (.Q(d_latch_2_q), .D(and_1_out), .CLK(or_1_out));  // open: Q0
  not not_2 (not_2_out, or_2_out);
  or or_2 (or_2_out, sr_latch_1_q, in_3);
  and and_2 (out_4, d_latch_2_q, not_2_out);
endmodule

module Set_Flip_Flop (
  input  CLK,
  input  D,
  input  Set,
  output Q
);

  wire or_1_out;

  or or_1 (or_1_out, D, Set);
  D_Flip_Flop d_flip_flop_1 (.Q(Q), .D(or_1_out), .CLK(CLK));
endmodule

module Set_async_D_Latch (
  input  CLK,
  input  SET,
  input  D,
  output Q,
  output Q0
);

  wire and_1_out, and_2_out, not_1_out, or_1_out;

  or or_1 (or_1_out, SET, D);
  and and_1 (and_1_out, CLK, not_1_out);
  not not_1 (not_1_out, or_1_out);
  and and_2 (and_2_out, CLK, or_1_out);
  SR_Latch sr_latch_1 (.Q0(Q0), .Q(Q), .S(and_2_out), .R(and_1_out));
endmodule

module async_set_Flip_Flop (
  input  CLK,
  input  D,
  input  Set,
  output Q
);

  wire not_1_out, set_async_d_latch_1_q;

  not not_1 (not_1_out, CLK);
  Set_async_D_Latch set_async_d_latch_1 (.Q(set_async_d_latch_1_q), .D(D), .SET(Set), .CLK(not_1_out));  // open: Q0
  Set_async_D_Latch set_async_d_latch_2 (.Q(Q), .D(set_async_d_latch_1_q), .SET(Set), .CLK(CLK));  // open: Q0
endmodule

module D_trigger (
  input  CLK,
  input  D,
  input  enable,
  input  set,
  input  reset,
  output out_6
);

  wire and_1_out, enabled_flip_flop_1_q, not_1_out, not_2_out, not_3_out, or_1_out, or_2_out,
       resettable_flip_flop_1_q, set_flip_flop_1_q;

  Enabled_Flip_Flop enabled_flip_flop_1 (.Q(enabled_flip_flop_1_q), .D(D), .EN(and_1_out), .CLK(CLK));
  and and_1 (and_1_out, enable, not_2_out);
  not not_1 (not_1_out, set);
  Set_Flip_Flop set_flip_flop_1 (.Q(set_flip_flop_1_q), .Set(not_3_out), .D(D), .CLK(CLK));
  not not_2 (not_2_out, or_1_out);
  or or_1 (or_1_out, not_3_out, reset);
  not not_3 (not_3_out, or_2_out);
  or or_2 (or_2_out, not_1_out, reset);
  Resettable_Flip_Flop resettable_flip_flop_1 (.Q(resettable_flip_flop_1_q), .RESET(reset), .D(D), .CLK(CLK));
  or or_3 (out_6, resettable_flip_flop_1_q, enabled_flip_flop_1_q, set_flip_flop_1_q);
endmodule
