// Logisim project zad_5_1_1.circ as structural Verilog: 9 circuits, main circuit PC
module PC (
  input  Reset,
  output [31:0] out_2
);

  wire clock_1_out;
  wire [31:0] adder_1_out;

  Adder #(.width(32)) adder_1 (.a(out_2), .b(32'h4), .out(adder_1_out));  // open: cin, cout
  Register #(.width(32)) register_1 (.D(adder_1_out), .en(clock_1_out), .clk(clock_1_out), .Q(out_2), .clr(Reset));
  Clock clock_1 (.out(clock_1_out));
endmodule

module PC_test (
  input  in_1
);

  wire [31:0] pc_1_out_2;

  PC pc_1 (.Reset(in_1), .out_2(pc_1_out_2));
  // MIPSProgramROM mipsprogramrom_1: pin names not known; wires that end beside it: pc_1_out_2

  // Notes on the sheet:
  //   contents of mipsprogramrom_1 (hex, n*v repeats v):
  //   ADDIU $2, $0, 0x38 ADDIU $3, $0, 0x8 ADDIU $4, $0, 0x2 ADDIU $5, $0, 0x1  SLTI $6, $2, 0xf SLTI $7,
  //   $3, 0x8 SLTI $8, $1, 0x80 SLTI $9, $2, 0x800
endmodule

module Decode (
  input  [31:0] in_1,
  output [5:0] opcode,
  output [25:0] addr,
  output [4:0] rs,
  output [4:0] rt,
  output [15:0] imm,
  output [4:0] rd,
  output [4:0] shamt,
  output [5:0] funct
);


  assign addr = in_1[25:0];
  assign funct = in_1[5:0];
  assign imm = in_1[15:0];
  assign opcode = in_1[31:26];
  assign rd = in_1[15:11];
  assign rs = in_1[25:21];
  assign rt = in_1[20:16];
  assign shamt = in_1[10:6];
endmodule

module ControlV23232 (
  input  in_1
);

  wire clock_1_out, ExOp, RegWrite, slt_1_y, SLTOp, SLTu;
  wire [3:0] ALUOp;
  wire [4:0] rs, rt;
  wire [31:0] bit_extender_1_out, bitextend_1_out_3, mips_alu_1_p5, mipsprogramrom_1_p2, pc_1_out_2,
       registerfile_1_p6, Res;

  PC pc_1 (.Reset(in_1), .out_2(pc_1_out_2));
  Clock clock_1 (.out(clock_1_out));
  // RegisterFile registerfile_1: pin names not known; wires that end beside it: Res, clock_1_out, RegWrite, rt, rs, registerfile_1_p6
  // MIPSProgramROM mipsprogramrom_1: pin names not known; wires that end beside it: pc_1_out_2, {mipsprogramrom_1_p2[31:26], rs, rt, mipsprogramrom_1_p2[15:0]}
  BitExtend bitextend_1 (.imm(mipsprogramrom_1_p2[15:0]), .ExOp(ExOp), .out_3(bitextend_1_out_3));
  // Mips_ALU mips_alu_1: pin names not known; wires that end beside it: registerfile_1_p6, bitextend_1_out_3, ALUOp, registerfile_1_p6, mips_alu_1_p5
  SLT slt_1 (.A(registerfile_1_p6), .B(bitextend_1_out_3), .U(SLTu), .y(slt_1_y));
  Control control_1 (
    .opcode(mipsprogramrom_1_p2[31:26]), .ALUOper(ALUOp), .RegistrWrite(RegWrite), .ExOper(ExOp),
    .SLTOper(SLTOp), .SLTu(SLTu));
  Multiplexer #(.width(32), .enable("false")) multiplexer_1 (
    .in0(mips_alu_1_p5), .in1(bit_extender_1_out), .out(Res), .sel(SLTOp));
  assign bit_extender_1_out = {{31{1'b0}}, slt_1_y};  // Bit_Extender bit_extender_1

  // Notes on the sheet:
  //   contents of mipsprogramrom_1 (hex, n*v repeats v):
  //   ADDIU $2, $zero, -10912 ADDIU $3, $zero, -16837 ADDIU $4, $zero, 24393  SLTIU $5, $1, -20799 SLTIU
  //   $6, $2, -10912 SLTIU $7, $3, -16837 SLTI $8, $4, 24393  SLTIU $5, $2, 10230 SLTI $6, $3, -8073 SLTIU
  //   $7, $2, 25708 SLTIU $8, $2, 9393 SLTIU $9, $1, 9388 SLTIU $10, $3, 9030 SLTI $11, $1, -13847 SLTIU
  //   $12, $3, 24515 SLTI $13, $3, 12504 SLTIU $14, $2, 6849 SLTIU $15, $3, -9869 SLTI $16, $2, -21317
  //   SLTI $17, $3, -13736 SLTIU $18, $2, 2119 SLTIU $19, $3, -26589 SLTI $20, $2, -27763 SLTIU $21, $1,
  //   -14958 SLTIU $22, $2, 3806 SLTI $23, $1, -29446 SLTIU $24, $3, -23798 SLTI $25, $3, 29416 SLTI $26,
  //   $2, 8412 SLTIU $27, $2, -14859 SLTI $28, $1, 21251 SLTI $29, $2, -635 SLTI $30, $2, 28461
endmodule

module ALUOp (
  input  x5,
  input  x4,
  input  x3,
  input  x2,
  input  x1,
  input  x0,
  output a3,
  output a2,
  output a1,
  output a0
);

  wire and_1_out, and_2_out, and_3_out, and_4_out, and_5_out, not_1_out, not_2_out, not_3_out, not_4_out,
       not_5_out;

  not not_1 (not_1_out, x3);
  not not_2 (not_2_out, x1);
  not not_3 (not_3_out, x5);
  not not_4 (not_4_out, x4);
  not not_5 (not_5_out, x2);
  and and_1 (and_1_out, not_1_out, x0);
  and and_2 (and_2_out, not_2_out, x0);
  and and_3 (and_3_out, x2, x0);
  and and_4 (and_4_out, x4, x0);
  and and_5 (and_5_out, x5, x0);
  and and_6 (a0, not_3_out, not_4_out, x3, not_5_out, x1, x0);
  or or_1 (a1, and_1_out, and_2_out, and_3_out, and_4_out, and_5_out);

  assign a2 = x1;
  assign a3 = x2;
endmodule

module RegWrite (
  input  x5,
  input  x4,
  input  x3,
  input  x2,
  input  x1,
  input  x0,
  output RegWrite,
  output ExOp,
  output SLTOp,
  output SLTu
);

  wire not_2_out, not_3_out, not_4_out;

  not not_1 (ExOp, x2);
  not not_2 (not_2_out, x5);
  not not_3 (not_3_out, x4);
  not not_4 (not_4_out, x2);
  and and_1 (SLTOp, not_2_out, not_3_out, x3, not_4_out, x1);

  assign RegWrite = 1'b1;
  assign SLTu = x0;
endmodule

module Control (
  input  [5:0] opcode,
  output [3:0] ALUOper,
  output RegistrWrite,
  output ExOper,
  output SLTOper,
  output SLTu
);

  ALUOp aluop_1 (
    .x5(opcode[5]), .x4(opcode[4]), .x3(opcode[3]), .x2(opcode[2]), .x1(opcode[1]), .x0(opcode[0]),
    .a3(ALUOper[3]), .a2(ALUOper[2]), .a1(ALUOper[1]), .a0(ALUOper[0]));
  RegWrite regwrite_1 (
    .x5(opcode[5]), .x4(opcode[4]), .x3(opcode[3]), .x2(opcode[2]), .x1(opcode[1]), .x0(opcode[0]),
    .RegWrite(RegistrWrite), .ExOp(ExOper), .SLTOp(SLTOper), .SLTu(SLTu));
endmodule

module BitExtend (
  input  [15:0] imm,
  input  ExOp,
  output [31:0] out_3
);

  wire [31:0] bit_extender_1_out, bit_extender_2_out;

  assign bit_extender_1_out = {{16{1'b0}}, imm};  // Bit_Extender bit_extender_1
  assign bit_extender_2_out = {{16{imm[15]}}, imm};  // Bit_Extender bit_extender_2
  Multiplexer #(.width(32), .enable("false")) multiplexer_1 (
    .in0(bit_extender_1_out), .in1(bit_extender_2_out), .out(out_3), .sel(ExOp));
endmodule

module SLT (
  input  [31:0] A,
  input  [31:0] B,
  input  U,
  output y
);

  wire comparator_1_lt, comparator_2_lt;

  Comparator #(.width(32)) comparator_1 (.a(A), .b(B), .lt(comparator_1_lt));  // open: gt, eq
  Comparator #(.width(32), .mode("unsigned")) comparator_2 (.a(A), .b(B), .lt(comparator_2_lt));  // open: gt, eq
  Multiplexer #(.enable("false")) multiplexer_1 (.in0(comparator_1_lt), .in1(comparator_2_lt), .out(y), .sel(U));
endmodule
