// Logisim project zad_5_1_2.circ as structural Verilog: 13 circuits, main circuit PC
module PC (
  input  Reset,
  output [31:0] out_2
);

  wire clock_1_out;
  wire [31:0] adder_1_out;

  Adder #(.width(32)) adder_1 (.a(out_2), .b(32'h4), .out(adder_1_out));  // open: cin, cout
  Register #(.width(32)) register_1 (.D(adder_1_out), .en(clock_1_out), .clk(clock_1_out), .Q(out_2), .clr(Reset));
  Clock clock_1 (.out(clock_1_out));
endmodule

module PC_test (
  input  in_1
);

  wire [31:0] pc_1_out_2;

  PC pc_1 (.Reset(in_1), .out_2(pc_1_out_2));
  // MIPSProgramROM mipsprogramrom_1: pin names not known; wires that end beside it: pc_1_out_2

  // Notes on the sheet:
  //   contents of mipsprogramrom_1 (hex, n*v repeats v):
  //   ADDIU $2, $0, 0x38 ADDIU $3, $0, 0x8 ADDIU $4, $0, 0x2 ADDIU $5, $0, 0x1  SLTI $6, $2, 0xf SLTI $7,
  //   $3, 0x8 SLTI $8, $1, 0x80 SLTI $9, $2, 0x800
endmodule

module Decode (
  input  [31:0] in_1,
  output [5:0] opcode,
  output [25:0] addr,
  output [4:0] rs,
  output [4:0] rt,
  output [15:0] imm,
  output [4:0] rd,
  output [4:0] shamt,
  output [5:0] funct
);


  assign addr = in_1[25:0];
  assign funct = in_1[5:0];
  assign imm = in_1[15:0];
  assign opcode = in_1[31:26];
  assign rd = in_1[15:11];
  assign rs = in_1[25:21];
  assign rt = in_1[20:16];
  assign shamt = in_1[10:6];
endmodule

module ControlV23232 (
  input  in_1
);

  wire ALUSrc, and_1_out, and_2_out, and_3_out, clock_1_out, ExOp, IsMove, LUI, MoveZ, not_1_out, or_1_out,
       RegDst, RegWrite, slt_1_y, SLTOp, SLTu, V, WasMoved, xor_1_out;
  wire [3:0] ALUOp;
  wire [4:0] bitselector_1_out, rd, rdrt, rs, rt, SA, shamt;
  wire [5:0] funct, opcode;
  wire [15:0] lmm;
  wire [25:0] addr;
  wire [31:0] A, B, bit_extender_1_out, bitextend_1_out_3, logicalshifter_1_o, mips_alu_1_p6,
       mipsprogramrom_1_p2, multiplexer_2_out, multiplexer_3_out, multiplexer_4_out, multiplexer_6_out,
       pc_1_out_2, Res;

  PC pc_1 (.Reset(in_1), .out_2(pc_1_out_2));
  Clock clock_1 (.out(clock_1_out));
  and and_1 (and_1_out, RegWrite, or_1_out);
  // RegisterFile registerfile_1: pin names not known; wires that end beside it: Res, clock_1_out, and_1_out, rdrt, rs, rt, A, B
  or or_1 (or_1_out, WasMoved, not_1_out);
  not not_1 (not_1_out, IsMove);
  // MIPSProgramROM mipsprogramrom_1: pin names not known; wires that end beside it: pc_1_out_2, mipsprogramrom_1_p2
  Multiplexer #(.width(5), .enable("false")) multiplexer_1 (.in0(rt), .in1(rd), .out(rdrt), .sel(xor_1_out));
  xor xor_1 (xor_1_out, RegDst, and_2_out);
  and and_2 (and_2_out, WasMoved, IsMove);
  Decode decode_1 (
    .in_1(mipsprogramrom_1_p2), .opcode(opcode), .addr(addr), .rs(rs), .rt(rt), .imm(lmm), .rd(rd),
    .shamt(shamt), .funct(funct));
  BitExtend bitextend_1 (.imm(lmm), .ExOp(ExOp), .out_3(bitextend_1_out_3));
  Multiplexer #(.width(32), .enable("false")) multiplexer_2 (
    .in0(bitextend_1_out_3), .in1(B), .out(multiplexer_2_out), .sel(ALUSrc));
  Multiplexer #(.width(32), .enable("false")) multiplexer_3 (
    .in0(bitextend_1_out_3), .in1(B), .out(multiplexer_3_out), .sel(ALUSrc));
  // Mips_ALU mips_alu_1: pin names not known; wires that end beside it: A, multiplexer_3_out, A, ALUOp, SA, mips_alu_1_p6
  SLT slt_1 (.A(A), .B(multiplexer_2_out), .U(SLTu), .y(slt_1_y));
  Control control_1 (
    .func(funct), .opcode(opcode), .ALUOper(ALUOp), .RegistrWrite(RegWrite), .ExOper(ExOp), .SLTOper(SLTOp),
    .SLTu(SLTu), .RegDst(RegDst), .ALUSrc(ALUSrc), .IsMove(IsMove), .MoveZ(MoveZ), .LUI(LUI), .V(V));
  assign bit_extender_1_out = {{31{1'b0}}, slt_1_y};  // Bit_Extender bit_extender_1
  mov mov_1 (.rt(B), .MoveZ(MoveZ), .wasMoved(WasMoved));
  Multiplexer #(.width(32), .enable("false")) multiplexer_4 (
    .in0(mips_alu_1_p6), .in1(bit_extender_1_out), .out(multiplexer_4_out), .sel(SLTOp));
  Multiplexer #(.width(5), .enable("false")) multiplexer_5 (.in0(shamt), .in1(bitselector_1_out), .out(SA), .sel(V));
  BitSelector #(.width(32), .group(5)) bitselector_1 (.in(A), .out(bitselector_1_out), .sel(3'b000));
  Multiplexer #(.width(32), .enable("false")) multiplexer_6 (
    .in0(multiplexer_4_out), .in1(A), .out(multiplexer_6_out), .sel(and_3_out));
  and and_3 (and_3_out, WasMoved, IsMove);
  Multiplexer #(.width(32), .enable("false")) multiplexer_7 (
    .in0(multiplexer_6_out), .in1(logicalshifter_1_o), .out(Res), .sel(LUI));
  logicalShifter logicalshifter_1 (.O(logicalshifter_1_o), .inp(lmm));

  // Notes on the sheet:
  //   contents of mipsprogramrom_1 (hex, n*v repeats v):
  //   LUI $1, 33848 LUI $2, 74 LUI $3, 56045 LUI $4, 27330 LUI $5, 15254 LUI $6, 37593 LUI $7, 15517 LUI
  //   $8, 6457 LUI $9, 27493 LUI $10, 65378 LUI $11, 39311 LUI $12, 3604 LUI $13, 65518 LUI $14, 1988 LUI
  //   $15, 57851 LUI $16, 34065 LUI $17, 56700 LUI $18, 36303 LUI $19, 56033 LUI $20, 47686 LUI $21, 44708
  //   LUI $22, 17702 LUI $23, 9308 LUI $24, 21814 LUI $25, 49082 LUI $26, 27503 LUI $27, 25174 LUI $28,
  //   65475 LUI $29, 39676 LUI $30, 6595 LUI $31, 33220 ORI $4, $4, 0xbeef ORI $5, $5, 0xd00d ORI $6, $6,
  //   0xabba ORI $7, $7, 0xc0de ORI $8, $8, 0xbeef ORI $9, $9, 0xface ORI $10, $10, 0xdec0 ORI $11, $11,
  //   0xfe0d
endmodule

module ALUOp (
  input  x5,
  input  x4,
  input  x3,
  input  x2,
  input  x1,
  input  x0,
  output a3,
  output a2,
  output a1,
  output a0
);

  wire and_1_out, and_2_out, and_3_out, and_4_out, and_5_out, and_6_out, and_7_out, and_8_out, and_9_out,
       and_10_out, not_1_out, not_2_out, not_3_out, not_4_out, not_5_out, not_6_out, not_7_out, not_8_out,
       not_9_out;

  not not_1 (not_1_out, x5);
  not not_2 (not_2_out, x4);
  not not_3 (not_3_out, x1);
  not not_4 (not_4_out, x5);
  not not_5 (not_5_out, x4);
  not not_6 (not_6_out, x3);
  not not_7 (not_7_out, x5);
  not not_8 (not_8_out, x4);
  not not_9 (not_9_out, x2);
  and and_1 (and_1_out, not_1_out, not_2_out, x3, x1);
  and and_2 (and_2_out, x3, x2);
  and and_3 (and_3_out, x4, x2);
  and and_4 (and_4_out, x5, x2);
  and and_5 (and_5_out, not_3_out, x0);
  and and_6 (and_6_out, x3, x0);
  and and_7 (and_7_out, x4, x0);
  and and_8 (and_8_out, x5, x0);
  and and_9 (and_9_out, not_4_out, not_5_out, not_6_out, x1, x0);
  and and_10 (and_10_out, not_7_out, not_8_out, x3, not_9_out, x1);
  or or_1 (a3, and_1_out, and_2_out, and_3_out, and_4_out);
  or or_2 (a1, and_5_out, and_6_out, and_7_out, and_8_out);
  or or_3 (a0, and_9_out, and_10_out);

  assign a2 = x1;
endmodule

module RegWrite (
  input  x5,
  input  x4,
  input  x3,
  input  x2,
  input  x1,
  input  x0,
  output RegWrite,
  output ExOp,
  output SLTOp,
  output SLTu,
  output RegDst,
  output ALUSrc
);

  wire and_2_out, and_3_out, and_4_out, and_5_out, and_6_out, and_7_out, and_8_out, not_2_out, not_3_out,
       not_4_out, not_5_out, not_6_out, not_7_out, not_8_out, not_9_out, not_10_out, not_11_out, not_12_out,
       not_13_out, not_14_out, not_15_out;

  not not_1 (ExOp, x2);
  not not_2 (not_2_out, x4);
  not not_3 (not_3_out, x2);
  not not_4 (not_4_out, x4);
  not not_5 (not_5_out, x2);
  not not_6 (not_6_out, x5);
  not not_7 (not_7_out, x4);
  not not_8 (not_8_out, x3);
  not not_9 (not_9_out, x0);
  not not_10 (not_10_out, x5);
  not not_11 (not_11_out, x4);
  not not_12 (not_12_out, x3);
  not not_13 (not_13_out, x4);
  not not_14 (not_14_out, x4);
  and and_1 (SLTOp, not_2_out, x3, not_3_out, x1);
  not not_15 (not_15_out, x3);
  and and_2 (and_2_out, x5, not_4_out, not_5_out, x1);
  and and_3 (and_3_out, not_6_out, not_7_out, not_8_out, not_9_out);
  and and_4 (and_4_out, not_10_out, not_11_out, not_12_out, x1);
  and and_5 (and_5_out, x4, x3);
  and and_6 (and_6_out, x5, not_13_out, x0);
  and and_7 (and_7_out, x5, not_14_out, x2);
  and and_8 (and_8_out, x5, x3);
  or or_1 (RegDst, not_15_out, and_2_out);
  or or_2 (ALUSrc, and_3_out, and_4_out, and_5_out, and_6_out, and_7_out, and_8_out);

  assign RegWrite = 1'b1;
  assign SLTu = x0;
endmodule

module Control (
  input  [5:0] func,
  input  [5:0] opcode,
  output [3:0] ALUOper,
  output RegistrWrite,
  output ExOper,
  output SLTOper,
  output SLTu,
  output RegDst,
  output ALUSrc,
  output IsMove,
  output MoveZ,
  output LUI,
  output V
);

  wire isopcodezero_1_iszero, not_1_out;
  wire [5:0] multiplexer_1_out;

  not not_1 (not_1_out, isopcodezero_1_iszero);
  isOpCodeZero isopcodezero_1 (.isZero(isopcodezero_1_iszero), .opcode(opcode));
  Multiplexer #(.width(6), .enable("false")) multiplexer_1 (
    .in0(func), .in1(opcode), .out({multiplexer_1_out[5:3], V, multiplexer_1_out[1:0]}), .sel(not_1_out));
  ALUOp aluop_1 (
    .x5(multiplexer_1_out[5]), .x4(multiplexer_1_out[4]), .x3(multiplexer_1_out[3]), .x2(V),
    .x1(multiplexer_1_out[1]), .x0(multiplexer_1_out[0]), .a3(ALUOper[3]), .a2(ALUOper[2]), .a1(ALUOper[1]),
    .a0(ALUOper[0]));
  RegWrite regwrite_1 (
    .x5(multiplexer_1_out[5]), .x4(multiplexer_1_out[4]), .x3(multiplexer_1_out[3]), .x2(V),
    .x1(multiplexer_1_out[1]), .x0(multiplexer_1_out[0]), .RegWrite(RegistrWrite), .ExOp(ExOper),
    .SLTOp(SLTOper), .SLTu(SLTu), .RegDst(RegDst), .ALUSrc(ALUSrc));
  // Move move_1: pin names not known; wires that end beside it: multiplexer_1_out[5], multiplexer_1_out[4], multiplexer_1_out[3], V, multiplexer_1_out[1], multiplexer_1_out[0], opcode, IsMove, MoveZ, LUI
endmodule

module BitExtend (
  input  [15:0] imm,
  input  ExOp,
  output [31:0] out_3
);

  wire [31:0] bit_extender_1_out, bit_extender_2_out;

  assign bit_extender_1_out = {{16{1'b0}}, imm};  // Bit_Extender bit_extender_1
  assign bit_extender_2_out = {{16{imm[15]}}, imm};  // Bit_Extender bit_extender_2
  Multiplexer #(.width(32), .enable("false")) multiplexer_1 (
    .in0(bit_extender_1_out), .in1(bit_extender_2_out), .out(out_3), .sel(ExOp));
endmodule

module SLT (
  input  [31:0] A,
  input  [31:0] B,
  input  U,
  output y
);

  wire comparator_1_lt, comparator_2_lt;

  Comparator #(.width(32)) comparator_1 (.a(A), .b(B), .lt(comparator_1_lt));  // open: gt, eq
  Comparator #(.width(32), .mode("unsigned")) comparator_2 (.a(A), .b(B), .lt(comparator_2_lt));  // open: gt, eq
  Multiplexer #(.enable("false")) multiplexer_1 (.in0(comparator_1_lt), .in1(comparator_2_lt), .out(y), .sel(U));
endmodule

module isOpCodeZero (
  input  [5:0] opcode,
  output isZero
);

  wire or_1_out;

  not not_1 (isZero, or_1_out);
  or or_1 (or_1_out, opcode[0], opcode[1], opcode[2], opcode[3], opcode[4], opcode[5]);
endmodule

module Move (
  input  x5,
  input  x4,
  input  x3,
  input  x2,
  input  x1,
  input  x0,
  input  [5:0] x,
  output isMove,
  output MoveZ,
  output LUI
);

  wire and_1_out, isopcodezero_1_iszero, not_1_out, not_2_out, not_3_out, not_4_out, not_5_out;

  not not_1 (not_1_out, x5);
  not not_2 (not_2_out, x4);
  not not_3 (not_3_out, x2);
  isOpCodeZero isopcodezero_1 (.isZero(isopcodezero_1_iszero), .opcode(x));
  and and_1 (and_1_out, not_1_out, not_2_out, x3, not_3_out, x1);
  not not_4 (not_4_out, x0);
  not not_5 (not_5_out, not_3_out);
  and and_2 (isMove, and_1_out, isopcodezero_1_iszero);
  and and_3 (MoveZ, not_4_out, isopcodezero_1_iszero);
  and and_4 (LUI, not_1_out, not_2_out, x3, not_5_out, x1, x0);
endmodule

module mov (
  input  [31:0] rt,
  input  MoveZ,
  output wasMoved
);

  wire comparator_1_eq, comparator_1_gt, comparator_1_lt, or_1_out;

  Comparator #(.width(32), .mode("unsigned")) comparator_1 (
    .a(rt), .b({32{1'b0}}), .gt(comparator_1_gt), .eq(comparator_1_eq), .lt(comparator_1_lt));
  or or_1 (or_1_out, comparator_1_gt, comparator_1_lt);
  Multiplexer #(.enable("false")) multiplexer_1 (.in0(or_1_out), .in1(comparator_1_eq), .out(wasMoved), .sel(MoveZ));
endmodule

module logicalShifter (
  input  [15:0] inp,
  output [31:0] O
);

  assign {O[15:0], O[31:16]} = {{16{1'b0}}, inp};  // Bit_Extender bit_extender_1
endmodule
