// Logisim project zad_5_1_2_BETATEST.circ as structural Verilog: 18 circuits, main circuit PC
module PC (
  input  Reset,
  output [31:0] out_2
);

  wire clock_1_out;
  wire [31:0] adder_1_out;

  Adder #(.width(32)) adder_1 (.a(out_2), .b(32'h4), .out(adder_1_out));  // open: cin, cout
  Register #(.width(32)) register_1 (.D(adder_1_out), .en(clock_1_out), .clk(clock_1_out), .Q(out_2), .clr(Reset));
  Clock clock_1 (.out(clock_1_out));
endmodule

module PC_test (
  input  in_1
);

  wire [31:0] pc_1_out_2;

  PC pc_1 (.Reset(in_1), .out_2(pc_1_out_2));
  // MIPSProgramROM mipsprogramrom_1: pin names not known; wires that end beside it: pc_1_out_2

  // Notes on the sheet:
  //   contents of mipsprogramrom_1 (hex, n*v repeats v):
  //   ADDIU $2, $0, 0x38 ADDIU $3, $0, 0x8 ADDIU $4, $0, 0x2 ADDIU $5, $0, 0x1  SLTI $6, $2, 0xf SLTI $7,
  //   $3, 0x8 SLTI $8, $1, 0x80 SLTI $9, $2, 0x800
endmodule

module Decode (
  input  [31:0] in_1,
  output [5:0] opcode,
  output [25:0] addr,
  output [4:0] rs,
  output [4:0] rt,
  output [15:0] imm,
  output [4:0] rd,
  output [4:0] shamt,
  output [5:0] funct
);


  assign addr = in_1[25:0];
  assign funct = in_1[5:0];
  assign imm = in_1[15:0];
  assign opcode = in_1[31:26];
  assign rd = in_1[15:11];
  assign rs = in_1[25:21];
  assign rt = in_1[20:16];
  assign shamt = in_1[10:6];
endmodule

module ControlV23232 (
  input  reset
);

  wire ALUSrc, and_1_out, and_2_out, and_3_out, BEQ, BGTA, BLEZ, BNE, BTAC, clock_1_out, clock_2_out,
       clock_3_out, ExOp, IsBE, IsJump, IsMove, JR, JRL, LUI, LW, MoveZ, not_1_out, or_1_out, RegDst,
       RegWrite, slt_1_y, SLTOp, SLTu, SW, V, WasMoved, xor_1_out;
  wire [3:0] ALUOp;
  wire [4:0] bitselector_1_out, multiplexer_1_out, rd, rdrt, rs, rt, SA, shamt;
  wire [5:0] funct, opcode;
  wire [15:0] lmm;
  wire [25:0] addr;
  wire [31:0] A, adder_1_out, B, bit_extender_1_out, bit_extender_2_out, bitextend_1_out_3,
       bitextend_2_out_3, logicalshifter_1_o, LWRes, mips_alu_1_p4, mips_alu_2_p6, mipsprogramrom_1_p2,
       multiplexer_3_out, multiplexer_4_out, multiplexer_6_out, multiplexer_7_out, multiplexer_8_out,
       multiplexer_9_out, PC, Res;

  Clock clock_1 (.out(clock_1_out));
  Multiplexer #(.width(5), .enable("false")) multiplexer_1 (
    .in0(rt), .in1(rd), .out(multiplexer_1_out), .sel(xor_1_out));
  xor xor_1 (xor_1_out, RegDst, and_1_out);
  PC2 pc2_1 (
    .clk(clock_1_out), .jmp(IsJump), .reset(reset), .instr(addr), .A(A[25:0]), .JR(JR), .BTAC(BTAC),
    .imm(lmm), .addr(PC));
  Clock clock_2 (.out(clock_2_out));
  and and_1 (and_1_out, WasMoved, IsMove);
  and and_2 (and_2_out, RegWrite, or_1_out);
  or or_1 (or_1_out, WasMoved, not_1_out);
  Multiplexer #(.width(5), .enable("false")) multiplexer_2 (
    .in0(multiplexer_1_out), .in1({5{1'b1}}), .out(rdrt), .sel(JRL));
  not not_1 (not_1_out, IsMove);
  // MIPSProgramROM mipsprogramrom_1: pin names not known; wires that end beside it: PC, mipsprogramrom_1_p2
  // RegisterFile registerfile_1: pin names not known; wires that end beside it: Res, clock_2_out, and_2_out, rdrt, rs, rt, A, B
  Decode decode_1 (
    .in_1(mipsprogramrom_1_p2), .opcode(opcode), .addr(addr), .rs(rs), .rt(rt), .imm(lmm), .rd(rd),
    .shamt(shamt), .funct(funct));
  BitExtend bitextend_1 (.imm(lmm), .ExOp(ExOp), .out_3(bitextend_1_out_3));
  mov mov_1 (.rt(B), .MoveZ(MoveZ), .wasMoved(WasMoved));
  Control control_1 (
    .func(funct), .opcode(opcode), .ALUOper(ALUOp), .RegistrWrite(RegWrite), .ExOper(ExOp), .SLTOper(SLTOp),
    .SLTu(SLTu), .RegDst(RegDst), .ALUSrc(ALUSrc), .IsMove(IsMove), .MoveZ(MoveZ), .LUI(LUI), .V(V),
    .IsJump(IsJump), .JR(JR), .JRL(JRL), .BEQ(BEQ), .BNE(BNE), .IsBE(IsBE), .BLEZ(BLEZ), .BGTA(BGTA),
    .LW(LW), .SW(SW));
  BitExtend bitextend_2 (.imm(lmm), .ExOp(ExOp), .out_3(bitextend_2_out_3));
  Multiplexer #(.width(32), .enable("false")) multiplexer_3 (
    .in0(bitextend_1_out_3), .in1(B), .out(multiplexer_3_out), .sel(ALUSrc));
  assign bit_extender_1_out = {{16{lmm[15]}}, lmm};  // Bit_Extender bit_extender_1
  Multiplexer #(.width(32), .enable("false")) multiplexer_4 (
    .in0(bitextend_2_out_3), .in1(B), .out(multiplexer_4_out), .sel(ALUSrc));
  // Mips_ALU mips_alu_1: pin names not known; wires that end beside it: A, bit_extender_1_out, 4'b1010, mips_alu_1_p4
  // Mips_ALU mips_alu_2: pin names not known; wires that end beside it: A, multiplexer_4_out, A, ALUOp, SA, mips_alu_2_p6
  SLT slt_1 (.A(A), .B(multiplexer_3_out), .U(SLTu), .y(slt_1_y));
  BitSelector #(.width(32), .group(5)) bitselector_1 (.in(A), .out(bitselector_1_out), .sel(3'b000));
  assign bit_extender_2_out = {{31{1'b0}}, slt_1_y};  // Bit_Extender bit_extender_2
  Multiplexer #(.width(5), .enable("false")) multiplexer_5 (.in0(shamt), .in1(bitselector_1_out), .out(SA), .sel(V));
  Multiplexer #(.width(32), .enable("false")) multiplexer_6 (
    .in0(mips_alu_2_p6), .in1(bit_extender_2_out), .out(multiplexer_6_out), .sel(SLTOp));
  Clock clock_3 (.out(clock_3_out));
  Multiplexer #(.width(32), .enable("false")) multiplexer_7 (
    .in0(multiplexer_6_out), .in1(A), .out(multiplexer_7_out), .sel(and_3_out));
  and and_3 (and_3_out, WasMoved, IsMove);
  // MIPS_RAM #(.addrWidth(24)) mips_ram_1: pin names not known; wires that end beside it: mips_alu_1_p4[23:0], B, SW, clock_3_out, LW, LWRes
  logicalShifter logicalshifter_1 (.O(logicalshifter_1_o), .inp(lmm));
  Multiplexer #(.width(32), .enable("false")) multiplexer_8 (
    .in0(multiplexer_7_out), .in1(logicalshifter_1_o), .out(multiplexer_8_out), .sel(LUI));
  Multiplexer #(.width(32), .enable("false")) multiplexer_9 (
    .in0(multiplexer_8_out), .in1(adder_1_out), .out(multiplexer_9_out), .sel(JRL));
  Adder #(.width(32)) adder_1 (.a(PC), .b(32'h4), .out(adder_1_out));  // open: cin, cout
  Multiplexer #(.width(32), .enable("false")) multiplexer_10 (
    .in0(multiplexer_9_out), .in1(LWRes), .out(Res), .sel(LW));
  EQBlock eqblock_1 (.BNE(BNE), .BEQ(BEQ), .B(B), .BLEZ(BLEZ), .IsBE(IsBE), .A(A), .BGTZ(BGTA), .BTA(BTAC));

  // Notes on the sheet:
  //   contents of mipsprogramrom_1 (hex, n*v repeats v):
  //   sw $t1, -100($t2) sw $t1, -100($t2) lw $t3, -100($t2)
endmodule

module ALUOp (
  input  x5,
  input  x4,
  input  x3,
  input  x2,
  input  x1,
  input  x0,
  output a3,
  output a2,
  output a1,
  output a0
);

  wire and_1_out, and_2_out, and_3_out, and_4_out, and_5_out, and_6_out, and_7_out, and_8_out, and_9_out,
       and_10_out, not_1_out, not_2_out, not_3_out, not_4_out, not_5_out, not_6_out, not_7_out, not_8_out,
       not_9_out;

  not not_1 (not_1_out, x5);
  not not_2 (not_2_out, x4);
  not not_3 (not_3_out, x1);
  not not_4 (not_4_out, x5);
  not not_5 (not_5_out, x4);
  not not_6 (not_6_out, x3);
  not not_7 (not_7_out, x5);
  not not_8 (not_8_out, x4);
  not not_9 (not_9_out, x2);
  and and_1 (and_1_out, not_1_out, not_2_out, x3, x1);
  and and_2 (and_2_out, x3, x2);
  and and_3 (and_3_out, x4, x2);
  and and_4 (and_4_out, x5, x2);
  and and_5 (and_5_out, not_3_out, x0);
  and and_6 (and_6_out, x3, x0);
  and and_7 (and_7_out, x4, x0);
  and and_8 (and_8_out, x5, x0);
  and and_9 (and_9_out, not_4_out, not_5_out, not_6_out, x1, x0);
  and and_10 (and_10_out, not_7_out, not_8_out, x3, not_9_out, x1);
  or or_1 (a3, and_1_out, and_2_out, and_3_out, and_4_out);
  or or_2 (a1, and_5_out, and_6_out, and_7_out, and_8_out);
  or or_3 (a0, and_9_out, and_10_out);

  assign a2 = x1;
endmodule

module RegWrite (
  input  x5,
  input  x4,
  input  x3,
  input  x2,
  input  x1,
  input  x0,
  output RegWrite,
  output ExOp,
  output SLTOp,
  output SLTu,
  output RegDst,
  output ALUSrc
);

  wire and_1_out, and_2_out, and_3_out, and_4_out, and_5_out, and_6_out, and_7_out, and_8_out, and_9_out,
       and_10_out, and_11_out, and_13_out, and_14_out, and_15_out, and_16_out, and_17_out, and_18_out,
       and_19_out, and_20_out, and_21_out, and_22_out, and_23_out, and_24_out, not_1_out, not_2_out,
       not_3_out, not_4_out, not_5_out, not_6_out, not_7_out, not_8_out, not_9_out, not_10_out, not_11_out,
       not_12_out, not_13_out, not_14_out, not_15_out, not_16_out, not_17_out, not_18_out, not_19_out,
       not_20_out, not_21_out, not_22_out, not_23_out, not_24_out, not_25_out, not_26_out, not_27_out,
       not_28_out, not_29_out, not_30_out, not_31_out, not_32_out, not_33_out, not_34_out, not_35_out,
       not_36_out, not_37_out;

  not not_1 (not_1_out, x3);
  not not_2 (not_2_out, x1);
  not not_3 (not_3_out, x5);
  not not_4 (not_4_out, x0);
  not not_5 (not_5_out, x3);
  not not_6 (not_6_out, x1);
  not not_7 (not_7_out, x0);
  not not_8 (not_8_out, x3);
  not not_9 (not_9_out, x2);
  not not_10 (not_10_out, x1);
  not not_11 (not_11_out, x2);
  not not_12 (not_12_out, x2);
  not not_13 (not_13_out, x2);
  not not_14 (not_14_out, x2);
  not not_15 (not_15_out, x4);
  not not_16 (not_16_out, x2);
  not not_17 (not_17_out, x3);
  not not_18 (not_18_out, x1);
  not not_19 (not_19_out, x5);
  not not_20 (not_20_out, x3);
  not not_21 (not_21_out, x3);
  not not_22 (not_22_out, x3);
  not not_23 (not_23_out, x3);
  not not_24 (not_24_out, x0);
  not not_25 (not_25_out, x4);
  not not_26 (not_26_out, x2);
  not not_27 (not_27_out, x5);
  not not_28 (not_28_out, x4);
  not not_29 (not_29_out, x3);
  not not_30 (not_30_out, x1);
  not not_31 (not_31_out, x0);
  not not_32 (not_32_out, x4);
  not not_33 (not_33_out, x3);
  not not_34 (not_34_out, x4);
  not not_35 (not_35_out, x3);
  not not_36 (not_36_out, x0);
  not not_37 (not_37_out, x4);
  and and_1 (and_1_out, not_1_out, not_2_out);
  and and_2 (and_2_out, not_3_out, x0);
  and and_3 (and_3_out, x3, x1, not_4_out);
  and and_4 (and_4_out, x5, not_5_out);
  and and_5 (and_5_out, x5, not_6_out);
  and and_6 (and_6_out, x5, not_7_out);
  and and_7 (and_7_out, not_8_out, not_9_out, not_10_out);
  and and_8 (and_8_out, not_11_out, x0);
  and and_9 (and_9_out, x3, not_12_out, x1);
  and and_10 (and_10_out, x4, not_13_out);
  and and_11 (and_11_out, x5, not_14_out);
  and and_12 (SLTOp, not_15_out, x3, not_16_out, x1);
  and and_13 (and_13_out, not_17_out, not_18_out);
  and and_14 (and_14_out, not_19_out, not_20_out, x0);
  and and_15 (and_15_out, not_21_out, x2);
  and and_16 (and_16_out, x4, not_22_out);
  and and_17 (and_17_out, x5, not_23_out, not_24_out);
  and and_18 (and_18_out, x5, not_25_out, x3, not_26_out, x1);
  and and_19 (and_19_out, not_27_out, not_28_out, not_29_out, not_30_out, not_31_out);
  and and_20 (and_20_out, not_32_out, not_33_out, x1, x0);
  and and_21 (and_21_out, not_34_out, not_35_out, x2, not_36_out);
  and and_22 (and_22_out, x4, x3);
  and and_23 (and_23_out, x5, not_37_out, x0);
  and and_24 (and_24_out, x5, x3);
  or or_1 (RegWrite, and_1_out, and_2_out, x2, and_3_out, x4, and_4_out, and_5_out, and_6_out);
  or or_2 (ExOp, and_7_out, and_8_out, and_9_out, and_10_out, and_11_out);
  or or_3 (RegDst, and_13_out, and_14_out, and_15_out, and_16_out, and_17_out, and_18_out);
  or or_4 (ALUSrc, and_19_out, and_20_out, and_21_out, and_22_out, and_23_out, and_24_out);

  assign SLTu = x0;
endmodule

module Control (
  input  [5:0] func,
  input  [5:0] opcode,
  output [3:0] ALUOper,
  output RegistrWrite,
  output ExOper,
  output SLTOper,
  output SLTu,
  output RegDst,
  output ALUSrc,
  output IsMove,
  output MoveZ,
  output LUI,
  output V,
  output IsJump,
  output JR,
  output JRL,
  output BEQ,
  output BNE,
  output IsBE,
  output BLEZ,
  output BGTA,
  output LW,
  output SW
);

  wire isopcodezero_1_iszero, not_1_out;
  wire [5:0] multiplexer_1_out;

  not not_1 (not_1_out, isopcodezero_1_iszero);
  isOpCodeZero isopcodezero_1 (.isZero(isopcodezero_1_iszero), .opcode(opcode));
  Multiplexer #(.width(6), .enable("false")) multiplexer_1 (
    .in0(func), .in1(opcode), .out({multiplexer_1_out[5:3], V, multiplexer_1_out[1:0]}), .sel(not_1_out));
  ALUOp aluop_1 (
    .x5(multiplexer_1_out[5]), .x4(multiplexer_1_out[4]), .x3(multiplexer_1_out[3]), .x2(V),
    .x1(multiplexer_1_out[1]), .x0(multiplexer_1_out[0]), .a3(ALUOper[3]), .a2(ALUOper[2]), .a1(ALUOper[1]),
    .a0(ALUOper[0]));
  RegWrite regwrite_1 (
    .x5(multiplexer_1_out[5]), .x4(multiplexer_1_out[4]), .x3(multiplexer_1_out[3]), .x2(V),
    .x1(multiplexer_1_out[1]), .x0(multiplexer_1_out[0]), .RegWrite(RegistrWrite), .ExOp(ExOper),
    .SLTOp(SLTOper), .SLTu(SLTu), .RegDst(RegDst), .ALUSrc(ALUSrc));
  Move move_1 (
    .x0(multiplexer_1_out[0]), .x4(multiplexer_1_out[4]), .x5(multiplexer_1_out[5]),
    .x1(multiplexer_1_out[1]), .x3(multiplexer_1_out[3]), .isMove(IsMove), .x2(V), .MoveZ(MoveZ), .LUI(LUI),
    .x(opcode));
  JType jtype_1 (
    .x5(multiplexer_1_out[5]), .x4(multiplexer_1_out[4]), .x3(multiplexer_1_out[3]), .x2(V),
    .x1(multiplexer_1_out[1]), .x0(multiplexer_1_out[0]), .x(opcode), .isJump(IsJump), .JR(JR), .JRL(JRL));
  BrEq breq_1 (
    .x5(multiplexer_1_out[5]), .x4(multiplexer_1_out[4]), .x3(multiplexer_1_out[3]), .x2(V),
    .x1(multiplexer_1_out[1]), .x0(multiplexer_1_out[0]), .BEQ(BEQ), .BNE(BNE), .IsBE(IsBE), .BLEZ(BLEZ),
    .BGTA(BGTA));
  DataMemory datamemory_1 (
    .x5(multiplexer_1_out[5]), .x4(multiplexer_1_out[4]), .x3(multiplexer_1_out[3]), .x2(V),
    .x1(multiplexer_1_out[1]), .x0(multiplexer_1_out[0]), .LW(LW), .SW(SW));
endmodule

module BitExtend (
  input  [15:0] imm,
  input  ExOp,
  output [31:0] out_3
);

  wire [31:0] bit_extender_1_out, bit_extender_2_out;

  assign bit_extender_1_out = {{16{1'b0}}, imm};  // Bit_Extender bit_extender_1
  assign bit_extender_2_out = {{16{imm[15]}}, imm};  // Bit_Extender bit_extender_2
  Multiplexer #(.width(32), .enable("false")) multiplexer_1 (
    .in0(bit_extender_1_out), .in1(bit_extender_2_out), .out(out_3), .sel(ExOp));
endmodule

module SLT (
  input  [31:0] A,
  input  [31:0] B,
  input  U,
  output y
);

  wire comparator_1_lt, comparator_2_lt;

  Comparator #(.width(32)) comparator_1 (.a(A), .b(B), .lt(comparator_1_lt));  // open: gt, eq
  Comparator #(.width(32), .mode("unsigned")) comparator_2 (.a(A), .b(B), .lt(comparator_2_lt));  // open: gt, eq
  Multiplexer #(.enable("false")) multiplexer_1 (.in0(comparator_1_lt), .in1(comparator_2_lt), .out(y), .sel(U));
endmodule

module isOpCodeZero (
  input  [5:0] opcode,
  output isZero
);

  wire or_1_out;

  not not_1 (isZero, or_1_out);
  or or_1 (or_1_out, opcode[0], opcode[1], opcode[2], opcode[3], opcode[4], opcode[5]);
endmodule

module Move (
  input  x5,
  input  x4,
  input  x3,
  input  x2,
  input  x1,
  input  x0,
  input  [5:0] x,
  output isMove,
  output MoveZ,
  output LUI
);

  wire and_1_out, isopcodezero_1_iszero, not_1_out, not_2_out, not_3_out, not_4_out, not_5_out;

  not not_1 (not_1_out, x5);
  not not_2 (not_2_out, x4);
  not not_3 (not_3_out, x2);
  isOpCodeZero isopcodezero_1 (.isZero(isopcodezero_1_iszero), .opcode(x));
  not not_4 (not_4_out, x0);
  not not_5 (not_5_out, not_3_out);
  and and_1 (and_1_out, not_1_out, not_2_out, x3, not_3_out, x1);
  and and_2 (isMove, and_1_out, isopcodezero_1_iszero);
  and and_3 (MoveZ, not_4_out, isopcodezero_1_iszero);
  and and_4 (LUI, not_1_out, not_2_out, x3, not_5_out, x1, x0);
endmodule

module mov (
  input  [31:0] rt,
  input  MoveZ,
  output wasMoved
);

  wire comparator_1_eq, not_1_out;

  Comparator #(.width(32), .mode("unsigned")) comparator_1 (
    .a(rt), .b({32{1'b0}}), .eq(comparator_1_eq));  // open: gt, lt
  not not_1 (not_1_out, comparator_1_eq);
  Multiplexer #(.enable("false")) multiplexer_1 (.in0(not_1_out), .in1(comparator_1_eq), .out(wasMoved), .sel(MoveZ));
endmodule

module logicalShifter (
  input  [15:0] inp,
  output [31:0] O
);

  assign {O[15:0], O[31:16]} = {{16{1'b0}}, inp};  // Bit_Extender bit_extender_1
endmodule

module JType (
  input  x5,
  input  x4,
  input  x3,
  input  x2,
  input  x1,
  input  x0,
  input  [5:0] x,
  output isJump,
  output JR,
  output JRL
);

  wire aboba, and_1_out, and_2_out, and_3_out, and_4_out, and_5_out, not_1_out, not_2_out, not_3_out,
       not_4_out, not_5_out, not_6_out, not_7_out, not_8_out, not_9_out, not_10_out, not_11_out, not_12_out,
       not_13_out, not_14_out, not_15_out, not_16_out, not_17_out, not_18_out, not_19_out, not_20_out,
       not_21_out, not_22_out, not_23_out, not_24_out, not_25_out, not_26_out;

  isOpCodeZero isopcodezero_1 (.isZero(aboba), .opcode(x));
  not not_1 (not_1_out, x5);
  not not_2 (not_2_out, x4);
  not not_3 (not_3_out, x3);
  not not_4 (not_4_out, x2);
  not not_5 (not_5_out, x0);
  not not_6 (not_6_out, aboba);
  and and_1 (and_1_out, not_1_out, not_2_out, not_3_out, not_4_out, x1, not_5_out, not_6_out);
  not not_7 (not_7_out, x5);
  not not_8 (not_8_out, x4);
  not not_9 (not_9_out, x3);
  not not_10 (not_10_out, x2);
  not not_11 (not_11_out, x0);
  not not_12 (not_12_out, aboba);
  not not_13 (not_13_out, x5);
  not not_14 (not_14_out, x4);
  not not_15 (not_15_out, x2);
  not not_16 (not_16_out, x1);
  not not_17 (not_17_out, x0);
  not not_18 (not_18_out, x5);
  not not_19 (not_19_out, x4);
  not not_20 (not_20_out, x3);
  not not_21 (not_21_out, x2);
  not not_22 (not_22_out, aboba);
  not not_23 (not_23_out, x5);
  not not_24 (not_24_out, x4);
  not not_25 (not_25_out, x2);
  not not_26 (not_26_out, x1);
  and and_2 (and_2_out, not_7_out, not_8_out, not_9_out, not_10_out, x1, not_11_out, not_12_out);
  and and_3 (and_3_out, not_13_out, not_14_out, x3, not_15_out, not_16_out, not_17_out, aboba);
  and and_4 (and_4_out, not_18_out, not_19_out, not_20_out, not_21_out, x1, x0, not_22_out);
  and and_5 (and_5_out, not_23_out, not_24_out, x3, not_25_out, not_26_out, x0, aboba);
  or or_1 (isJump, and_2_out, and_3_out, and_4_out);
  or or_2 (JR, and_3_out, and_5_out);
  or or_3 (JRL, and_4_out, and_5_out);
endmodule

module PC2 (
  input  clk,
  input  jmp,
  input  reset,
  input  [25:0] instr,
  input  [25:0] A,
  input  JR,
  input  BTAC,
  input  [15:0] imm,
  output [31:0] addr
);

  wire [27:0] bit_extender_1_out, bit_extender_2_out, multiplexer_1_out, shifter_1_out;
  wire [31:0] bit_extender_3_out, BTA, multiplexer_2_out, multiplexer_3_out, P4, shifter_2_out;

  Adder #(.width(32)) adder_1 (.a(addr), .b(32'h4), .out(P4));  // open: cin, cout
  assign bit_extender_1_out = {{2{1'b0}}, instr};  // Bit_Extender bit_extender_1
  Multiplexer #(.width(28), .enable("false")) multiplexer_1 (
    .in0(shifter_1_out), .in1(bit_extender_2_out), .out(multiplexer_1_out), .sel(JR));
  Shifter #(.width(28)) shifter_1 (.in(bit_extender_1_out), .\dist (5'b00010), .out(shifter_1_out));
  assign bit_extender_2_out = {{2{1'b0}}, A};  // Bit_Extender bit_extender_2
  Multiplexer #(.width(32), .enable("false")) multiplexer_2 (
    .in0(P4), .in1({P4[31:28], multiplexer_1_out}), .out(multiplexer_2_out), .sel(jmp));
  assign bit_extender_3_out = {{16{imm[15]}}, imm};  // Bit_Extender bit_extender_3
  Shifter #(.width(32)) shifter_2 (.in(bit_extender_3_out), .\dist (5'b00010), .out(shifter_2_out));
  Multiplexer #(.width(32), .enable("false")) multiplexer_3 (
    .in0(multiplexer_2_out), .in1(BTA), .out(multiplexer_3_out), .sel(BTAC));
  Adder #(.width(32)) adder_2 (.a(shifter_2_out), .b(P4), .out(BTA));  // open: cin, cout
  Register #(.width(32)) register_1 (.D(multiplexer_3_out), .en(clk), .clk(clk), .Q(addr), .clr(reset));
endmodule

module BrEq (
  input  x5,
  input  x4,
  input  x3,
  input  x2,
  input  x1,
  input  x0,
  output BEQ,
  output BNE,
  output IsBE,
  output BLEZ,
  output BGTA
);

  wire and_1_out, not_1_out, not_2_out, not_3_out, not_4_out, not_5_out, not_6_out, not_7_out, not_8_out,
       not_9_out, not_10_out, not_11_out, not_12_out, not_13_out, not_14_out, not_15_out, not_16_out,
       not_17_out, not_18_out, not_19_out, not_20_out, not_21_out, not_22_out;

  not not_1 (not_1_out, x5);
  not not_2 (not_2_out, x4);
  not not_3 (not_3_out, x3);
  not not_4 (not_4_out, x2);
  not not_5 (not_5_out, x1);
  not not_6 (not_6_out, x0);
  and and_1 (and_1_out, not_1_out, not_2_out, not_3_out, not_4_out, not_5_out, not_6_out);
  not not_7 (not_7_out, x5);
  not not_8 (not_8_out, x4);
  not not_9 (not_9_out, x3);
  not not_10 (not_10_out, x1);
  not not_11 (not_11_out, x0);
  not not_12 (not_12_out, x5);
  not not_13 (not_13_out, x4);
  not not_14 (not_14_out, x3);
  not not_15 (not_15_out, x1);
  not not_16 (not_16_out, x5);
  not not_17 (not_17_out, x4);
  not not_18 (not_18_out, x3);
  not not_19 (not_19_out, x0);
  not not_20 (not_20_out, x5);
  not not_21 (not_21_out, x4);
  not not_22 (not_22_out, x3);
  and and_2 (BEQ, not_7_out, not_8_out, not_9_out, x2, not_10_out, not_11_out);
  and and_3 (BNE, not_12_out, not_13_out, not_14_out, x2, not_15_out, x0);
  and and_4 (BLEZ, not_16_out, not_17_out, not_18_out, x2, x1, not_19_out);
  and and_5 (BGTA, not_20_out, not_21_out, not_22_out, x2, x1, x0);
  or or_1 (IsBE, BEQ, BNE, BLEZ, BGTA);
endmodule

module EQBlock (
  input  IsBE,
  input  [31:0] A,
  input  BEQ,
  input  BNE,
  input  BLEZ,
  input  BGTZ,
  input  [31:0] B,
  output BTA
);

  wire BGTZ_t, BLEZ_t, EQ, multiplexer_1_out, multiplexer_2_out, multiplexer_3_out, NEQ;

  Comparator #(.width(32)) comparator_1 (.a(A), .b(B), .eq(EQ));  // open: gt, lt
  Comparator #(.width(32)) comparator_2 (.a(A), .b({32{1'b0}}), .lt(BLEZ_t));  // open: gt, eq
  not not_1 (NEQ, EQ);
  not not_2 (BGTZ_t, BLEZ_t);
  Multiplexer #(.enable("false")) multiplexer_1 (.in0(IsBE), .in1(EQ), .out(multiplexer_1_out), .sel(BEQ));
  Multiplexer #(.enable("false")) multiplexer_2 (
    .in0(multiplexer_1_out), .in1(NEQ), .out(multiplexer_2_out), .sel(BNE));
  Multiplexer #(.enable("false")) multiplexer_3 (
    .in0(multiplexer_2_out), .in1(BLEZ_t), .out(multiplexer_3_out), .sel(BLEZ));
  Multiplexer #(.enable("false")) multiplexer_4 (.in0(multiplexer_3_out), .in1(BGTZ_t), .out(BTA), .sel(BGTZ));
endmodule

module DataMemory (
  input  x5,
  input  x4,
  input  x3,
  input  x2,
  input  x1,
  input  x0,
  output LW,
  output SW
);

  wire not_1_out, not_2_out, not_3_out, not_4_out, not_5_out;

  not not_1 (not_1_out, x4);
  not not_2 (not_2_out, x3);
  not not_3 (not_3_out, x2);
  not not_4 (not_4_out, x4);
  not not_5 (not_5_out, x2);
  and and_1 (LW, x5, not_1_out, not_2_out, not_3_out, x1, x0);
  and and_2 (SW, x5, not_4_out, x3, not_5_out, x1, x0);
endmodule
